// Logisim project DLD PROJECT.circ as structural Verilog: 1 circuit, main circuit main
module main (
  input  A1,
  input  B1,
  input  C1,
  input  D1,
  input  A2,
  input  B2,
  input  C2,
  input  D2,
  output X
);

  wire xnor_1_out, xnor_2_out, xnor_3_out, xnor_4_out;

  xnor xnor_1 (xnor_1_out, A1, A2);
  xnor xnor_2 (xnor_2_out, B1, B2);
  xnor xnor_3 (xnor_3_out, C1, C2);
  xnor xnor_4 (xnor_4_out, D1, D2);
  and and_1 (X, xnor_1_out, xnor_2_out, xnor_3_out, xnor_4_out);
  LED led_1 (.in(X));

  // Notes on the sheet:
  //   DOOR PASSWORD
  //   PASSWORD KEY-IN
endmodule
